// Logisim project Simulation.circ as structural Verilog: 5 circuits, main circuit main
module main (
  input  in_1,
  input  in_2,
  input  in_3,
  input  ON___OFF,
  input  in_5,
  output _0___AM___1___PM
);

  wire _12_HOUR_COUNTER_a0, _12_HOUR_COUNTER_b0, _12_HOUR_COUNTER_b1, _12_HOUR_COUNTER_b2,
       _12_HOUR_COUNTER_b3, and_1_out, and_2_out, BCD_TO_7_SEGMENT_2_a, BCD_TO_7_SEGMENT_2_b,
       BCD_TO_7_SEGMENT_2_c, BCD_TO_7_SEGMENT_2_d, BCD_TO_7_SEGMENT_2_e, BCD_TO_7_SEGMENT_2_f,
       BCD_TO_7_SEGMENT_2_g, BCD_TO_7_SEGMENT_3_a, BCD_TO_7_SEGMENT_3_b, BCD_TO_7_SEGMENT_3_c,
       BCD_TO_7_SEGMENT_3_d, BCD_TO_7_SEGMENT_3_e, BCD_TO_7_SEGMENT_3_f, BCD_TO_7_SEGMENT_3_g,
       BCD_TO_7_SEGMENT_4_a, BCD_TO_7_SEGMENT_4_b, BCD_TO_7_SEGMENT_4_c, BCD_TO_7_SEGMENT_4_d,
       BCD_TO_7_SEGMENT_4_e, BCD_TO_7_SEGMENT_4_f, BCD_TO_7_SEGMENT_4_g, BCD_TO_7_SEGMENT_a,
       BCD_TO_7_SEGMENT_b, BCD_TO_7_SEGMENT_c, BCD_TO_7_SEGMENT_d, BCD_TO_7_SEGMENT_e, BCD_TO_7_SEGMENT_f,
       BCD_TO_7_SEGMENT_g, clock_1_out, MOD_6_COUNTER_q0, MOD_6_COUNTER_q1, MOD_6_COUNTER_q2,
       MOD_6_COUNTER_z, MOD_10_COUNTER_d0_lsb, MOD_10_COUNTER_d1, MOD_10_COUNTER_d2, MOD_10_COUNTER_d3_msb,
       MOD_10_COUNTER_z, not_1_out, not_2_out, not_3_out;

  BCD_TO_7_SEGMENT BCD_TO_7_SEGMENT (
    .MSB_D3(in_1), .D2(in_1), .D1(in_1), .LSB_D0(_12_HOUR_COUNTER_a0), .A(BCD_TO_7_SEGMENT_a),
    .B(BCD_TO_7_SEGMENT_b), .C(BCD_TO_7_SEGMENT_c), .D(BCD_TO_7_SEGMENT_d), .E(BCD_TO_7_SEGMENT_e),
    .F(BCD_TO_7_SEGMENT_f), .G(BCD_TO_7_SEGMENT_g));
  and and_1 (and_1_out, MOD_10_COUNTER_z, MOD_6_COUNTER_z);
  Clock clock_1 (.out(clock_1_out));
  _7_Segment_Display u_7_segment_display_1 (
    .g(BCD_TO_7_SEGMENT_g), .f(BCD_TO_7_SEGMENT_f), .a(BCD_TO_7_SEGMENT_a), .b(BCD_TO_7_SEGMENT_b),
    .e(BCD_TO_7_SEGMENT_e), .d(BCD_TO_7_SEGMENT_d), .c(BCD_TO_7_SEGMENT_c));  // open: dp
  _7_Segment_Display u_7_segment_display_2 (
    .g(BCD_TO_7_SEGMENT_2_g), .f(BCD_TO_7_SEGMENT_2_f), .a(BCD_TO_7_SEGMENT_2_a), .b(BCD_TO_7_SEGMENT_2_b),
    .e(BCD_TO_7_SEGMENT_2_e), .d(BCD_TO_7_SEGMENT_2_d), .c(BCD_TO_7_SEGMENT_2_c), .dp(1'b1));
  BCD_TO_7_SEGMENT BCD_TO_7_SEGMENT_2 (
    .MSB_D3(_12_HOUR_COUNTER_b3), .D2(_12_HOUR_COUNTER_b2), .D1(_12_HOUR_COUNTER_b1),
    .LSB_D0(_12_HOUR_COUNTER_b0), .A(BCD_TO_7_SEGMENT_2_a), .B(BCD_TO_7_SEGMENT_2_b),
    .C(BCD_TO_7_SEGMENT_2_c), .D(BCD_TO_7_SEGMENT_2_d), .E(BCD_TO_7_SEGMENT_2_e), .F(BCD_TO_7_SEGMENT_2_f),
    .G(BCD_TO_7_SEGMENT_2_g));
  _12_Hour_Counter _12_HOUR_COUNTER (
    .Clk(clock_1_out), .Preset(in_3), .Enable(and_1_out), .Clear(in_5), .A0(_12_HOUR_COUNTER_a0),
    .B0(_12_HOUR_COUNTER_b0), .B1(_12_HOUR_COUNTER_b1), .B2(_12_HOUR_COUNTER_b2), .B3(_12_HOUR_COUNTER_b3));
  _7_Segment_Display u_7_segment_display_3 (
    .g(BCD_TO_7_SEGMENT_3_g), .f(BCD_TO_7_SEGMENT_3_f), .a(BCD_TO_7_SEGMENT_3_a), .b(BCD_TO_7_SEGMENT_3_b),
    .e(BCD_TO_7_SEGMENT_3_e), .d(BCD_TO_7_SEGMENT_3_d), .c(BCD_TO_7_SEGMENT_3_c));  // open: dp
  Mod_6_counter MOD_6_COUNTER (
    .Clk(clock_1_out), .Enable(MOD_10_COUNTER_z), ._1(1'b1), .Clear(in_5), .Preset(in_3),
    .q0(MOD_6_COUNTER_q0), .q1(MOD_6_COUNTER_q1), .q2(MOD_6_COUNTER_q2), .Z(MOD_6_COUNTER_z));
  _7_Segment_Display u_7_segment_display_4 (
    .g(BCD_TO_7_SEGMENT_4_g), .f(BCD_TO_7_SEGMENT_4_f), .a(BCD_TO_7_SEGMENT_4_a), .b(BCD_TO_7_SEGMENT_4_b),
    .e(BCD_TO_7_SEGMENT_4_e), .d(BCD_TO_7_SEGMENT_4_d), .c(BCD_TO_7_SEGMENT_4_c));  // open: dp
  BCD_TO_7_SEGMENT BCD_TO_7_SEGMENT_3 (
    .MSB_D3(in_2), .D2(MOD_6_COUNTER_q2), .D1(MOD_6_COUNTER_q1), .LSB_D0(MOD_6_COUNTER_q0),
    .A(BCD_TO_7_SEGMENT_3_a), .B(BCD_TO_7_SEGMENT_3_b), .C(BCD_TO_7_SEGMENT_3_c), .D(BCD_TO_7_SEGMENT_3_d),
    .E(BCD_TO_7_SEGMENT_3_e), .F(BCD_TO_7_SEGMENT_3_f), .G(BCD_TO_7_SEGMENT_3_g));
  MOD_10_COUNTER MOD_10_COUNTER (
    .clk(clock_1_out), .set(in_5), .enable(ON___OFF), .reset(in_3), .Z(MOD_10_COUNTER_z),
    .D3_MSB(MOD_10_COUNTER_d3_msb), .D2(MOD_10_COUNTER_d2), .D1(MOD_10_COUNTER_d1),
    .D0_LSB(MOD_10_COUNTER_d0_lsb));
  BCD_TO_7_SEGMENT BCD_TO_7_SEGMENT_4 (
    .MSB_D3(MOD_10_COUNTER_d3_msb), .D2(MOD_10_COUNTER_d2), .D1(MOD_10_COUNTER_d1),
    .LSB_D0(MOD_10_COUNTER_d0_lsb), .A(BCD_TO_7_SEGMENT_4_a), .B(BCD_TO_7_SEGMENT_4_b),
    .C(BCD_TO_7_SEGMENT_4_c), .D(BCD_TO_7_SEGMENT_4_d), .E(BCD_TO_7_SEGMENT_4_e), .F(BCD_TO_7_SEGMENT_4_f),
    .G(BCD_TO_7_SEGMENT_4_g));
  not not_1 (not_1_out, _12_HOUR_COUNTER_b2);
  not not_2 (not_2_out, _12_HOUR_COUNTER_b3);
  not not_3 (not_3_out, _12_HOUR_COUNTER_b1);
  T_Flip_Flop t_ff_1 (.clk(clock_1_out), .T(and_2_out), .Q(_0___AM___1___PM), .en(1'b1));  // open: Qn, preset, reset
  and and_2 (and_2_out, not_2_out, not_1_out, not_3_out, MOD_10_COUNTER_z, MOD_6_COUNTER_z, _12_HOUR_COUNTER_a0, _12_HOUR_COUNTER_b0);
endmodule

module Mod_6_counter (
  input  Clk,
  input  Enable,
  input  _1,
  input  Clear,
  input  Preset,
  output q0,
  output q1,
  output q2,
  output Z
);

  wire and_1_out, and_2_out, j_k_ff_1_qn;

  and and_1 (and_1_out, q0, q1);
  J_K_Flip_Flop j_k_ff_1 (
    .J(and_1_out), .clk(Clk), .K(q0), .Q(q2), .Qn(j_k_ff_1_qn), .preset(Preset), .en(Enable), .reset(Clear));
  J_K_Flip_Flop j_k_ff_2 (
    .J(and_2_out), .clk(Clk), .K(q0), .Q(q1), .preset(Preset), .en(Enable), .reset(Clear));  // open: Qn
  and and_2 (and_2_out, j_k_ff_1_qn, q0);
  J_K_Flip_Flop j_k_ff_3 (.J(_1), .clk(Clk), .K(_1), .Q(q0), .preset(Preset), .en(Enable), .reset(Clear));  // open: Qn
  and and_3 (Z, q2, q0);
endmodule

module _12_Hour_Counter (
  input  Clk,
  input  Preset,
  input  Enable,
  input  Clear,
  output A0,
  output B0,
  output B1,
  output B2,
  output B3
);

  wire and_1_out, and_2_out, and_3_out, and_4_out, and_5_out, and_6_out, and_8_out, and_9_out, and_10_out,
       and_11_out, d_ff_1_q, d_ff_1_qn, d_ff_2_qn, d_ff_3_q, d_ff_3_qn, d_ff_4_qn, or_1_out, or_2_out,
       xor_1_out;

  or or_1 (or_1_out, and_2_out, and_3_out, and_1_out);
  and and_1 (and_1_out, d_ff_4_qn, d_ff_1_q);
  and and_2 (and_2_out, B2, d_ff_3_q, B0);
  and and_3 (and_3_out, d_ff_3_qn, d_ff_1_q);
  D_Flip_Flop d_ff_1 (
    .clk(Clk), .D(or_1_out), .Q(d_ff_1_q), .Qn(d_ff_1_qn), .preset(Preset), .en(Enable), .reset(Clear));
  or or_2 (or_2_out, and_4_out, and_5_out, and_6_out);
  and and_4 (and_4_out, d_ff_1_qn, d_ff_2_qn, d_ff_3_q, B0);
  and and_5 (and_5_out, B2, d_ff_4_qn);
  and and_6 (and_6_out, B2, d_ff_3_qn);
  D_Flip_Flop d_ff_2 (.clk(Clk), .D(or_2_out), .Q(B2), .Qn(d_ff_2_qn), .preset(Preset), .en(Enable), .reset(Clear));
  xor xor_1 (xor_1_out, B0, d_ff_3_q);
  D_Flip_Flop d_ff_3 (
    .clk(Clk), .D(xor_1_out), .Q(d_ff_3_q), .Qn(d_ff_3_qn), .preset(Preset), .en(Enable), .reset(Clear));
  D_Flip_Flop d_ff_4 (.clk(Clk), .D(d_ff_4_qn), .Q(B0), .Qn(d_ff_4_qn), .preset(Preset), .en(Enable), .reset(Clear));
  and and_7 (B3, d_ff_1_q, d_ff_3_qn);
  and and_8 (and_8_out, d_ff_1_qn, d_ff_2_qn, d_ff_3_qn, d_ff_4_qn);
  and and_9 (and_9_out, d_ff_1_q, d_ff_3_q);
  and and_10 (and_10_out, d_ff_1_qn, d_ff_2_qn, d_ff_4_qn);
  and and_11 (and_11_out, d_ff_1_qn, d_ff_3_q);
  or or_3 (A0, and_8_out, and_9_out);
  or or_4 (B1, and_10_out, and_11_out);

  // Notes on the sheet:
  //   D3
  //   D2
  //   D1
  //   D0
endmodule

module BCD_TO_7_SEGMENT (
  input  MSB_D3,
  input  D2,
  input  D1,
  input  LSB_D0,
  output A,
  output B,
  output C,
  output D,
  output E,
  output F,
  output G
);

  wire and_1_out, and_2_out, and_3_out, and_4_out, and_5_out, and_6_out, and_7_out, and_8_out, and_9_out,
       and_10_out, not_1_out, not_2_out, not_3_out, not_4_out, not_5_out, not_6_out, not_7_out, not_8_out,
       not_9_out, not_10_out, not_11_out, xnor_1_out, xnor_2_out, xor_1_out;

  not not_1 (not_1_out, LSB_D0);
  not not_2 (not_2_out, D1);
  not not_3 (not_3_out, D2);
  not not_4 (not_4_out, LSB_D0);
  not not_5 (not_5_out, D2);
  not not_6 (not_6_out, LSB_D0);
  not not_7 (not_7_out, D2);
  not not_8 (not_8_out, D1);
  not not_9 (not_9_out, D2);
  not not_10 (not_10_out, LSB_D0);
  xnor xnor_1 (xnor_1_out, D2, LSB_D0);
  xnor xnor_2 (xnor_2_out, D1, LSB_D0);
  and and_1 (and_1_out, D1, not_4_out);
  and and_2 (and_2_out, not_5_out, not_6_out);
  and and_3 (and_3_out, not_7_out, D1);
  and and_4 (and_4_out, not_8_out, D2, LSB_D0);
  and and_5 (and_5_out, not_9_out, not_1_out);
  and and_6 (and_6_out, not_1_out, D1);
  and and_7 (and_7_out, not_1_out, D2);
  and and_8 (and_8_out, not_1_out, not_2_out);
  and and_9 (and_9_out, D2, not_2_out);
  xor xor_1 (xor_1_out, D1, D2);
  and and_10 (and_10_out, not_10_out, D1);
  not not_11 (not_11_out, D1);
  or or_1 (A, MSB_D3, xnor_1_out, D1);
  or or_2 (B, xnor_2_out, not_3_out);
  or or_3 (C, D2, not_11_out, LSB_D0);
  or or_4 (D, MSB_D3, and_1_out, and_2_out, and_3_out, and_4_out);
  or or_5 (E, and_5_out, and_6_out);
  or or_6 (F, and_7_out, MSB_D3, and_8_out, and_9_out);
  or or_7 (G, MSB_D3, xor_1_out, and_10_out);
endmodule

module MOD_10_COUNTER (
  input  clk,
  input  set,
  input  enable,
  input  reset,
  output Z,
  output D3_MSB,
  output D2,
  output D1,
  output D0_LSB
);

  wire and_2_out, and_3_out, and_4_out, and_5_out, j_k_ff_1_qn, not_1_out, not_2_out;

  and and_1 (Z, D3_MSB, not_2_out, not_1_out, D0_LSB);
  not not_1 (not_1_out, D1);
  not not_2 (not_2_out, D2);
  and and_2 (and_2_out, D2, D1, D0_LSB);
  J_K_Flip_Flop j_k_ff_1 (
    .J(and_2_out), .clk(clk), .K(D0_LSB), .Q(D3_MSB), .Qn(j_k_ff_1_qn), .preset(set), .en(enable),
    .reset(reset));
  and and_3 (and_3_out, D1, D0_LSB);
  J_K_Flip_Flop j_k_ff_2 (
    .J(and_3_out), .clk(clk), .K(and_5_out), .Q(D2), .preset(set), .en(enable), .reset(reset));  // open: Qn
  and and_4 (and_4_out, j_k_ff_1_qn, D0_LSB);
  J_K_Flip_Flop j_k_ff_3 (
    .J(and_4_out), .clk(clk), .K(D0_LSB), .Q(D1), .preset(set), .en(enable), .reset(reset));  // open: Qn
  and and_5 (and_5_out, D1, D0_LSB);
  J_K_Flip_Flop j_k_ff_4 (
    .J(1'b1), .clk(clk), .K(1'b1), .Q(D0_LSB), .preset(set), .en(enable), .reset(reset));  // open: Qn
endmodule
